// Logisim project 2X4DEC.circ as structural Verilog: 1 circuit, main circuit DEC2X4
module DEC2X4 (
  input  A,
  input  B,
  input  E,
  output Y3,
  output Y2,
  output Y1,
  output Y0
);

  wire NA, NB;

  not not_1 (NA, A);
  not not_2 (NB, B);
  and and_1 (Y3, A, B, E);
  and and_2 (Y2, A, NB, E);
  and and_3 (Y1, NA, B, E);
  and and_4 (Y0, NA, NB, E);
endmodule
