// Logisim project DEC3X8.circ as structural Verilog: 1 circuit, main circuit DEC3X8
module DEC3X8 (
  input  A,
  input  B,
  input  C,
  input  E,
  output Y7,
  output Y6,
  output Y5,
  output Y4,
  output Y3,
  output Y2,
  output Y1,
  output Y0
);

  wire NA, NB, NC;

  not not_1 (NA, A);
  not not_2 (NB, B);
  not not_3 (NC, C);
  and and_1 (Y7, A, B, C, E);
  and and_2 (Y6, A, B, NC, E);
  and and_3 (Y5, A, NB, C, E);
  and and_4 (Y4, A, NB, NC, E);
  and and_5 (Y3, NA, B, C, E);
  and and_6 (Y2, NA, B, NC, E);
  and and_7 (Y1, NA, NB, C, E);
  and and_8 (Y0, NA, NB, NC, E);
endmodule
